// Logisim project lab11.circ as structural Verilog
module Ex1 (
  input  [7:0] Input,
  output Out1,
  output [7:0] Out2
);

  and and_1 (Out1, Input[0], Input[7]);
  not not_1 (Out2[7], Input[7]);

  assign Out2[6:0] = Input[6:0];
endmodule

module rotr (
  input  [15:0] A,
  input  [3:0] B,
  output [15:0] Output
);

  Multiplier multiplier_1 ();  // open: a, b, out, cin, cout
  Divider divider_1 ();  // open: a, b, out, upper, rem
endmodule

module MUX (
  input  [15:0] in_1,
  input  [3:0] in_2,
  output out_3
);

  Multiplexer #(.select(4), .disabled(0), .enable("false")) multiplexer_1 (
    .in0(in_1[0]), .in1(in_1[1]), .in2(in_1[2]), .in3(in_1[3]), .in4(in_1[4]), .in5(in_1[5]), .in6(in_1[6]),
    .in7(in_1[7]), .in8(in_1[8]), .in9(in_1[9]), .in10(in_1[10]), .in11(in_1[11]), .in12(in_1[12]),
    .in13(in_1[13]), .in14(in_1[14]), .in15(in_1[15]), .out(out_3), .sel(in_2));
endmodule
